// Logisim project cpu_single_cycle.circ as structural Verilog
module main (
  input  CLK,
  input  Reset
);

  wire adder_3_p2, IMEM_p4, multiplexer_2_p3, RegFile_p3, RegFile_p4, RegFile_p5;
  wire [4:0] multiplexer_4_out;
  wire [31:0] DMEM_p3, PC_q;

  Register #(.width(32)) PC (.en(CLK), .Q(PC_q));  // open: D, clk, clr
  Multiplexer #(.width(32)) multiplexer_1 (.out(PC_q));  // open: in0, in1, sel, en
  // Adder #(.width(32)) adder_1: pin names not known; wires that end beside it: PC_q
  // Empty empty_1: pin names not known; wires that end beside it: PC_q
  // ROM #(.addrWidth(5), .dataWidth(32)) IMEM: pin names not known; wires that end beside it: CLK, Reset, PC_q, IMEM_p4
  // Adder #(.width(32)) adder_2: pin names not known; wires that end beside it: PC_q
  // Empty empty_2: pin names not known
  // Empty empty_3: pin names not known
  // RAM #(.addrWidth(5), .dataWidth(32)) RegFile: pin names not known; wires that end beside it: IMEM_p4, IMEM_p4, RegFile_p3, RegFile_p4, RegFile_p5
  // Multiplexer #(.width(32)) multiplexer_2: pin names not known; wires that end beside it: RegFile_p5, RegFile_p4, multiplexer_2_p3
  // Empty empty_4: pin names not known
  // Adder #(.width(32)) adder_3: pin names not known; wires that end beside it: multiplexer_2_p3, adder_3_p2
  // RAM #(.addrWidth(10), .dataWidth(32)) DMEM: pin names not known; wires that end beside it: multiplexer_2_p3, adder_3_p2, DMEM_p3
  Multiplexer #(.width(32)) multiplexer_3 (.out(DMEM_p3));  // open: in0, in1, sel, en
  Multiplexer #(.width(5)) multiplexer_4 (.out(multiplexer_4_out));  // open: in0, in1, sel, en
  // Probe on nothing
  // Probe on nothing
  // Probe on nothing
  // Probe on nothing

  // Notes on the sheet:
  //   contents of IMEM (hex, n*v repeats v):
  //   0: 012a5020 1: 012b5822 2: ac2a0000 3: 8c2c0000 4: 104c0001 5: 0 6: 14c5022 7: 0
endmodule

module ALU (
);

  Adder #(.width(32)) adder_1 ();  // open: a, b, out, cin, cout
  Subtractor #(.width(32)) subtractor_1 ();  // open: a, b, out, bin, bout
  Multiplexer #(.width(32), .select(2)) multiplexer_1 ();  // open: in0, in1, in2, in3, out, sel, en
endmodule
